# Fritzing sketch Hub (saved by Fritzing 0.9.2b)
breadboards: 1

parts:
  I2C_LCD1 = I2C_LCD [part_number=I2C_LCD chip_label=I2C_LCD package="DIP (Dual Inline) [THT]"]
  LCD1_20x5 = LCD screen  # not connected
  S1 = Round Pushbutton
  R1 = Resistor [tolerance=±5% resistance=220 package="2512 [SMD]"]
  R2 = Resistor [tolerance=±5% resistance=220 package="2512 [SMD]"]
  LED1 = DUO LED RG [package="5 mm [THT]"]

nets:
  N1: I2C_LCD1.GND, S1.leg1, R1.Pin_0, R2.Pin_0
  N2: R1.Pin_1, LED1.common_cathode

custom parts:
  I2C_LCD: I2C-Module to use a 1602 or 2004 LCD on with the wire.h libory Serial LCD Modul
  LCD screen: A standard character display, usually with 2x16 characters. Comes in many colors.
