# Fritzing sketch Sniffer (saved by Fritzing 0.9.2b)
circuit board: 8.46667cm x 5.64444cm
breadboards: 1

parts:
  R1 = Resistor [tolerance=±5% resistance=220 package="2512 [SMD]"]
  LED1 = DUO LED RG [package="5 mm [THT]"]
  U2 = atmega328 [package=dip]
  XTAL2 = Crystal [frequency="16 Mhz" package=THT]
  C5 = Ceramic Capacitor [capacitance=22pF voltage=50V package="100 mil [THT, multilayer]"]
  C6 = Ceramic Capacitor [capacitance=22pF voltage=50V package="100 mil [THT, multilayer]"]
  C4 = Electrolytic Capacitor [capacitance=1µF package="100 mil [THT, electrolytic]"]
  S2 = Round Pushbutton
  DHT1 = DHT11 Humitidy and Temperature Sensor (3 pins)
  I2C_LCD1 = I2C_LCD [part_number=I2C_LCD chip_label=I2C_LCD package="DIP (Dual Inline) [THT]"]
  R2 = Resistor [tolerance=±5% resistance=220 package="2512 [SMD]"]
  LCD1 = LCD screen  # not connected

nets:
  N1: R1.Pin_0, LED1.common_cathode
  VCC: LED1.green_anode, U2.VCC, U2.AVCC, U2.AREF, C4.+, DHT1.VCC, I2C_LCD1.VCC, R2.Pin_1
  N2: U2.RESET, R2.Pin_0
  GND: U2.GND, C5.1, C6.0, C4.-, S2.leg1, DHT1.GND, I2C_LCD1.GND
  N3: U2.XLAT1, XTAL2.pin_1, C5.0
  N4: U2.XLAT2, XTAL2.pin_0, C6.1
  N5: U2.D5_(PWM), DHT1.DATA

notes:
  DHT11
  Push-Button
  LCD I2C Module
  ESP8266 NodeMCU
  NovaFitness SDS011
  LED

custom parts:
  DHT11 Humitidy and Temperature Sensor (3 pins): DHT11 Humidity and Temperature Sensor (3 pins) from the design created by John De Cristofaro for Adafruit Industries.
  I2C_LCD: I2C-Module to use a 1602 or 2004 LCD on with the wire.h libory Serial LCD Modul
