# Fritzing sketch sniffer_v1 (saved by Fritzing 0.9.3b)
circuit board: 15.1629cm x 9.07213cm
breadboards: 1

parts:
  16Mhz1 = Crystal [frequency="16 Mhz" package=THT]
  ATMEL1 = atmega168 [package=dip]
  NOVA1 = Novafit SDS011
  C4 = Electrolytic Capacitor [capacitance=1µF package="100 mil [THT, electrolytic]"]
  C5 = Ceramic Capacitor [capacitance=100nF package="100 mil [THT, multilayer]"]
  C6 = Ceramic Capacitor [capacitance=100nF package="100 mil [THT, multilayer]"]
  10k1 = Resistor [tolerance=±5% resistance=220 package=THT]
  Q3 = DHT11 Module [package="TO92 [THT]"]
  WeMos_D1_Mini2 = WeMos D1 Mini
  R2 = Resistor [tolerance=±5% resistance=220 package=THT]
  Q4 = LED3Pins [package="TO92 [THT]"]
  RHT1 = LiquidDisplay
  Q5 = LED3Pins [package="TO92 [THT]"]
  R3 = Resistor [tolerance=±5% resistance=220 package=THT]
  C7 = Electrolytic Capacitor [capacitance=1µF package="100 mil [THT, electrolytic]"]
  C8 = Electrolytic Capacitor [capacitance=1µF package="100 mil [THT, electrolytic]"]

nets:
  N1: 16Mhz1.pin_0, ATMEL1.XLAT2, C6.1
  N2: 16Mhz1.pin_1, ATMEL1.XLAT1, C5.1
  N3: ATMEL1.RESET, 10k1.Pin_1
  VCC: ATMEL1.VCC, ATMEL1.AVCC, ATMEL1.AREF, NOVA1.Vcc, C4.-, 10k1.Pin_0, Q3.Vcc, WeMos_D1_Mini2.5V, RHT1.VCC, Q5.BLUE, C8.-
  GND: ATMEL1.GND, NOVA1.GND, C4.+, C5.0, C6.0, Q3.GND, WeMos_D1_Mini2.G, R2.Pin_0, RHT1.GND, R3.Pin_0, C7.+, C8.+
  N4: ATMEL1.D5_(PWM), Q3.Data
  N5: ATMEL1.D7, NOVA1.TX
  N6: ATMEL1.D8, NOVA1.RX
  N7: ATMEL1.D9_(PWM), WeMos_D1_Mini2.D7
  N8: ATMEL1.D10_(PWM), WeMos_D1_Mini2.D6
  N9: ATMEL1.D11_(PWM), Q4.BLUE
  N10: ATMEL1.D12, Q4.RED
  N11: WeMos_D1_Mini2.D1, RHT1.SCL
  N12: WeMos_D1_Mini2.D2, RHT1.SDA
  N13: WeMos_D1_Mini2.D4, C7.-
  N14: WeMos_D1_Mini2.D5, Q5.RED
  N15: R2.Pin_1, Q4.GND
  N16: Q5.GND, R3.Pin_1

custom parts:
  DHT11 Module: A standard PNP signal transistor
  LED3Pins: A standard NPN-transistor
